# Fritzing sketch sketch (saved by Fritzing 0.9.3b)
circuit board: 4.07204cm x 2.29866cm
breadboards: 1

parts:
  J2 = female pin header, 12 pins [form="♀ (female)"]
  J3 = female pin header, 16 pins [form="♀ (female)"]
  J4 = female pin header, 6 pins [form="♀ (female)"]
  J6 = female pin header, 3 pins [form="♀ (female)"]
  J5 = female pin header, 6 pins [form="♀ (female)"]

nets:
  N1: J2.pin3, J6.pin1, J5.pin1
  N2: J3.pin3, J4.pin1
  GND: J3.pin4, J4.pin2, J6.pin3, J5.pin2
  N3: J3.pin5, J4.pin3
  N4: J6.pin2, J5.pin3
